# Fritzing sketch Untitled Sketch (saved by Fritzing 0.9.10b)
breadboards: 1

parts:
  Part1 = Arduino Uno (Rev3)
  Potentiometer = POT [knob_status=0.1k% power=0.5W package=alps_pot]

nets:
  N1: Part1.A0, Potentiometer.S
  N2: Part1.GND, Potentiometer.A
  N3: Part1.5V, Potentiometer.E
