# Fritzing sketch practica-3 (saved by Fritzing 0.9.10b)
breadboards: 1

parts:
  Part1 = Arduino Uno (Rev3)
  Delay = POT [knob_status=50% power=0.5W package=alps_pot]
  LED = smd LED [color="Red (633nm)" package="0603 [SMD]"]

nets:
  N1: Part1.A0, Delay.S
  N2: Part1.D9_PWM, LED.anode
  N3: Part1.GND, Delay.A, LED.cathode
  N4: Part1.5V, Delay.E
