# Fritzing sketch practica-4 (saved by Fritzing 0.9.10b)
breadboards: 1

parts:
  R1 = Resistor [tolerance=±5% power=0.25 resistance=220 package=THT]
  R2 = Resistor [tolerance=±5% power=0.25 resistance=10000 package=THT]
  LED = LED - 5mm [color="Red (633nm)" current=0.030 package="5 mm [THT]"]
  Part1 = Arduino Uno (Rev3)
  BUTTON = Pushbutton [package="[THT]"]

nets (from the schematic view):
  N1: R1.Pin_0, Part1.D13/SCK
  N2: R1.Pin_1, LED.anode
  N3: R2.Pin_0, Part1.D2, BUTTON.Pin_1, BUTTON.Pin_2
  N4: R2.Pin_1, Part1.5V
  N5: LED.cathode, Part1.GND, BUTTON.Pin_3, BUTTON.Pin_4
