# Fritzing sketch practica-5 (saved by Fritzing 0.9.10b)
breadboards: 1

parts:
  LED = LED - 5mm [color="Red (633nm)" current=0.030 package="5 mm [THT]"]
  R1 = Resistor [tolerance=±5% power=0.25 resistance=220 package=THT]
  Part1 = Arduino Uno (Rev3)

nets:
  N1: LED.cathode, Part1.GND
  N2: LED.anode, R1.Pin_0
  N3: R1.Pin_1, Part1.D13/SCK
