# Fritzing sketch Untitled Sketch 9 (saved by Fritzing 0.9.10b)
breadboards: 1

parts:
  S1 = Pushbutton [package="[THT]"]
  R1 = Resistor [tolerance=±5% power=0.25 resistance=220 package=THT]
  Part1 = Arduino Uno (Rev3)
  LED1 = LED - 5mm [color="Red (633nm)" current=0.030 package="5 mm [THT]"]
  R2 = Resistor [tolerance=±5% power=0.25 resistance=220 package=THT]

nets:
  N1: S1.Pin_1, R1.Pin_0, Part1.D2
  N2: S1.Pin_3, Part1.GND, LED1.anode
  N3: R1.Pin_1, Part1.5V
  N4: Part1.D13/SCK, R2.Pin_0
  N5: LED1.cathode, R2.Pin_1
