# Fritzing sketch Untitled Sketch 10 (saved by Fritzing 0.9.10b)
breadboards: 1

parts:
  R1 = Resistor [tolerance=±5% power=0.25 resistance=220 package=THT]
  LED1 = LED - 5mm [color="Red (633nm)" current=0.030 package="5 mm [THT]"]
  Part1 = Arduino Uno (Rev3)

nets:
  N1: R1.Pin_0, Part1.D13/SCK
  N2: R1.Pin_1, LED1.cathode
  N3: LED1.anode, Part1.GND
