# Fritzing sketch Untitled Sketch 9 (saved by Fritzing 0.9.10b)
breadboards: 1

parts:
  S1 = Pushbutton [package="[THT]"]
  R1 = Resistor [tolerance=±5% power=0.25 resistance=220 package=THT]
  Part1 = Arduino Uno (Rev3)

nets:
  N1: S1.Pin_1, R1.Pin_0, Part1.D2
  N2: S1.Pin_3, Part1.GND
  N3: R1.Pin_1, Part1.5V
