# Fritzing sketch Untitled Sketch 8 (saved by Fritzing 0.9.10b)
breadboards: 1

parts:
  LED1 = smd LED [color="White (4500K)" package="0603 [SMD]"]
  R1 = Resistor [tolerance=±5% power=0.25 resistance=10k package=THT]
  R2 = Resistor [tolerance=±5% power=0.25 resistance=220 package=THT]
  Part1 = Arduino Uno (Rev3)
  LED3 = LED - 5mm [color="Green (555nm)" current=0.030 package="5 mm [THT]"]
  R3 = Resistor [tolerance=±5% power=0.25 resistance=220 package=THT]
  LED4 = smd LED [color="Infrared (940nm)" package="0603 [SMD]"]

nets:
  N1: LED1.cathode, R3.Pin_1
  N2: LED1.anode, R1.Pin_1, Part1.GND, LED3.anode
  N3: R1.Pin_0, Part1.D2, LED3.cathode, LED4.anode
  N4: R2.Pin_0, Part1.5V, R3.Pin_0
  N5: R2.Pin_1, LED4.cathode
